# Fritzing sketch Tattle_Phone_Circuit (saved by Fritzing 0.9.3b)

parts:
  MCU1 = Raspberry Pi Zero W
  LED1 = LED - 5mm [color="Red (633nm)" package="5 mm [THT]"]
  MIC1 = Microphone  # not connected
  S1 = Pushbutton [package=THT]
  part = Resistor [tolerance=±5% resistance=1k package=THT]

nets:
  N1: MCU1.pin_7, part.Pin_1
  N2: MCU1.pin_9, MCU1.pin_39, LED1.cathode, S1.leg1
  N3: MCU1.pin_11, S1.leg0
  N4: LED1.anode, part.Pin_0

notes:
  Status indicator
  USB
  Sound Card
  Telephone receiver switch
  Telephone receiver micriphone

custom parts:
  Raspberry Pi Zero W: The Raspberry Pi Zero is half the size of a Model A+, with twice the utility. A tiny Raspberry Pi that’s affordable enough for any project! · 1Ghz, Single-core CPU · 512MB RAM · Mini HDMI and USB On-The-Go ports · Micro USB power · HAT-compatible 40-pin header. Jan 2018: In this version schematic has been changed so the pins match the GPIO connector. I.e. the left hand pins are all the pins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
